// Logisim project prueba_generador.circ as structural Verilog: 1 circuit, main circuit Prueba_Generador
module Prueba_Generador (
  input  A,
  input  B,
  output AND_OUT,
  output OR_OUT,
  output XOR_OUT,
  output NOT_OUT
);

  and and_1 (AND_OUT, A, B);
  or or_1 (OR_OUT, A, B);
  xor xor_1 (XOR_OUT, A, B);
  not not_1 (NOT_OUT, A);
endmodule
