// Logisim project smips.circ as structural Verilog
module Board (
);

  wire CLK, HALT, MEM_WE, RESET, TTY_WE;
  wire [3:0] MEM_BE;
  wire [6:0] TTY_DATA;
  wire [31:0] MEM_ADDR, MEM_RDATA, MEM_WDATA;

  Clock Reloj (.out(CLK));
  Button u_Reset (.out(RESET));
  CPU cpu_1 (
    .CLK(CLK), .RESET(RESET), .MEM_RDATA(MEM_RDATA), .MEM_ADDR(MEM_ADDR), .MEM_WDATA(MEM_WDATA),
    .MEM_BE(MEM_BE), .MEM_WE(MEM_WE), .TTY_DATA(TTY_DATA), .TTY_WE(TTY_WE), .HALT(HALT));
  TTY #(.rows(12), .cols(48)) tty_1 (.data(TTY_DATA), .clk(CLK), .we(TTY_WE), .clr(RESET));
  Memory memory_1 (.CLK(CLK), .ADDR(MEM_ADDR), .WDATA(MEM_WDATA), .BE(MEM_BE), .WE(MEM_WE), .RDATA(MEM_RDATA));
  LED u_Halt (.in(HALT));

  // Notes on the sheet:
  //   S-MIPS | Board
  //   No modificar: la CPU se implementa dentro del subcircuito CPU.
endmodule

module CPU (
  input  CLK,
  input  RESET,
  input  [31:0] MEM_RDATA,
  output [31:0] MEM_ADDR,
  output [31:0] MEM_WDATA,
  output [3:0] MEM_BE,
  output MEM_WE,
  output [6:0] TTY_DATA,
  output TTY_WE,
  output HALT
);


  // Notes on the sheet:
  //   CPU S-MIPS: implementar aqui
  //   No cambiar nombres, anchos ni sentido de los pines: la placa depende de ellos.
endmodule

module Memory (
  input  CLK,
  input  [31:0] ADDR,
  input  [31:0] WDATA,
  input  [3:0] BE,
  input  WE,
  output [31:0] RDATA
);

  RAM #(.addrWidth(12), .dataWidth(32), .databus("bibus"), .byteenables("byteEnables"), .asyncread("true"), .\type ("nonvolatile")) Main_Memory (
    .addr(ADDR[13:2]), .we(WE), .oe(1'b1), .clk(CLK), .din(WDATA), .dout(RDATA), .be3(BE[3]), .be2(BE[2]),
    .be1(BE[1]), .be0(BE[0]));

  // Other names for the same wires on the sheet: A[11:0] = ADDR[13:2]

  // Notes on the sheet:
  //   Memoria unificada: 4096 palabras de 32 bits (16 KiB), little-endian
  //   Lectura combinacional; escritura en el flanco de subida de CLK con WE=1, solo en los bytes con BE=1.
  //   Se usan los bits 13..2 de ADDR; los demas se ignoran (el espacio se repite cada 16 KiB).
endmodule

module ALU (
  input  [31:0] A,
  input  [31:0] B,
  input  [2:0] ALU_OP,
  output [31:0] Y,
  output ZERO
);

  wire LT;
  wire [31:0] A_SIGN, ADD, AND, B_SIGN, OR, SLL, SLT, SRL, SUB;

  Adder #(.width(32)) adder_1 (.a(A), .b(B), .out(ADD));  // open: cin, cout
  assign OR = A | B;  // OR_Gate or_1, 32 bits wide
  Comparator #(.width(32)) comparator_1 (.a(A_SIGN), .b(B_SIGN), .lt(LT));  // open: gt, eq
  Shifter #(.width(32), .shift("lr")) shifter_1 (.in(A), .\dist (B[4:0]), .out(SRL));
  Comparator #(.width(32)) comparator_2 (.a(Y), .b({32{1'b0}}), .eq(ZERO));  // open: gt, lt
  Subtractor #(.width(32)) subtractor_1 (.a(A), .b(B), .out(SUB));  // open: bin, bout
  assign A_SIGN = A ^ 32'h80000000;  // XOR_Gate xor_1, 32 bits wide
  assign SLT = {{31{1'b0}}, LT};  // Bit_Extender bit_extender_1
  assign AND = A & B;  // AND_Gate and_1, 32 bits wide
  assign B_SIGN = B ^ 32'h80000000;  // XOR_Gate xor_2, 32 bits wide
  Shifter #(.width(32), .shift("ll")) shifter_2 (.in(A), .\dist (B[4:0]), .out(SLL));
  Multiplexer #(.width(32), .select(3)) multiplexer_1 (
    .in0(ADD), .in1(SUB), .in2(AND), .in3(OR), .in4(SLT), .in5(SLL), .in6(SRL), .in7({B[15:0], {16{1'b0}}}),
    .out(Y), .sel(ALU_OP));

  // Other names for the same wires on the sheet: B16[15:0] = B[15:0]; LUI[31:16] = B[15:0]; SHAMT[4:0] = B[4:0];
  //   MAIN[31:0] = Y
endmodule

module Datapath (
  input  CLK,
  input  RESET,
  input  [31:0] MEM_RDATA,
  input  PC_WRITE,
  input  [1:0] PC_SRC,
  input  IR_WRITE,
  input  A_WRITE,
  input  B_WRITE,
  input  ALU_WRITE,
  input  MDR_WRITE,
  input  REG_WRITE,
  input  RS1_SEL,
  input  RS2_SEL,
  input  [1:0] ALU_SRC_A,
  input  [1:0] ALU_SRC_B,
  input  [2:0] ALU_OP,
  input  MEM_ADDR_SEL,
  input  [1:0] EXT_TYPE,
  input  [1:0] REG_DST,
  input  [1:0] MEM_TO_REG,
  input  [1:0] MEM_SIZE,
  input  MEM_SIGNED,
  input  [1:0] JUMP_TYPE,
  input  MEM_WE,
  output [31:0] MEM_ADDR,
  output [31:0] MEM_WDATA,
  output [3:0] MEM_BE,
  output [31:0] IR,
  output [31:0] A,
  output [31:0] B,
  output ALU_ZERO,
  output [6:0] TTY_DATA
);

  wire [3:0] D_BYTE_MASK, D_MEM_BE_MASK;
  wire [4:0] RF_RD, RF_RS1, RF_RS2;
  wire [7:0] D_MDR_BYTE;
  wire [27:0] D_PC;
  wire [31:0] D_ALU_A, D_ALU_B, D_ALU_Y, D_ALUOUT, D_IMM, D_IMM_BRANCH, D_IMM_SEXT, D_IMM_SHAMT, D_IMM_ZEXT,
       D_LOAD_DATA, D_MDR, D_MDR_BYTE_EXT, D_MDR_BYTE_SEXT, D_MDR_BYTE_ZEXT, D_PC_NEXT, D_RD1, D_RD2, RF_WD;
  wire [31:28] D_JUMP_TARGET;

  Register_File register_file_1 (
    .CLK(CLK), .RESET(RESET), .RS1(RF_RS1), .RS2(RF_RS2), .RD(RF_RD), .WD(RF_WD), .REG_WRITE(REG_WRITE),
    .RD1(D_RD1), .RD2(D_RD2));
  Multiplexer #(.width(32), .select(2)) multiplexer_1 (
    .in0(D_ALU_Y), .in1(D_ALU_Y), .in2({D_JUMP_TARGET, IR[25:0], 2'b00}), .in3(A), .out(D_PC_NEXT),
    .sel(PC_SRC));
  Multiplexer #(.width(32), .select(2)) multiplexer_2 (
    .in0(A), .in1({D_JUMP_TARGET, D_PC}), .in2(B), .in3({32{1'b0}}), .out(D_ALU_A), .sel(ALU_SRC_A));
  Multiplexer #(.width(32), .select(2)) multiplexer_3 (
    .in0(B), .in1(D_IMM), .in2(32'h4), .in3({32{1'b0}}), .out(D_ALU_B), .sel(ALU_SRC_B));
  Multiplexer #(.width(32), .select(2)) multiplexer_4 (
    .in0(D_IMM_ZEXT), .in1(D_IMM_SEXT), .in2(D_IMM_SHAMT), .in3(D_IMM_BRANCH), .out(D_IMM), .sel(EXT_TYPE));
  Multiplexer #(.width(4), .select(2)) multiplexer_5 (
    .in0(4'b1111), .in1(D_BYTE_MASK), .in2(D_BYTE_MASK), .in3(D_BYTE_MASK), .out(D_MEM_BE_MASK),
    .sel(MEM_SIZE));
  assign D_IMM_ZEXT = {{16{1'b0}}, IR[15:0]};  // Bit_Extender bit_extender_1
  ALU alu_1 (.A(D_ALU_A), .B(D_ALU_B), .ALU_OP(ALU_OP), .Y(D_ALU_Y), .ZERO(ALU_ZERO));
  Multiplexer #(.width(5), .select(1)) multiplexer_6 (.in0(IR[25:21]), .in1(5'b00010), .out(RF_RS1), .sel(RS1_SEL));
  Multiplexer #(.width(32), .select(1)) multiplexer_7 (
    .in0({D_JUMP_TARGET, D_PC}), .in1(D_ALUOUT), .out(MEM_ADDR), .sel(MEM_ADDR_SEL));
  Multiplexer #(.width(5), .select(1)) multiplexer_8 (.in0(IR[20:16]), .in1(5'b00100), .out(RF_RS2), .sel(RS2_SEL));
  Multiplexer #(.width(8), .select(2)) multiplexer_9 (
    .in0(D_MDR[7:0]), .in1(D_MDR[15:8]), .in2(D_MDR[23:16]), .in3(D_MDR[31:24]), .out(D_MDR_BYTE),
    .sel(D_ALUOUT[1:0]));
  Shifter #(.width(32), .shift("ll")) shifter_1 (.in(D_IMM_SEXT), .\dist (5'b00010), .out(D_IMM_BRANCH));
  assign D_IMM_SEXT = {{16{IR[15]}}, IR[15:0]};  // Bit_Extender bit_extender_2
  Register #(.width(32)) PC (.D(D_PC_NEXT), .en(PC_WRITE), .clk(CLK), .Q({D_JUMP_TARGET, D_PC}), .clr(RESET));
  Register #(.width(32)) u_A (.D(D_RD1), .en(A_WRITE), .clk(CLK), .Q(A), .clr(RESET));
  Register #(.width(32)) ALUOUT (.D(D_ALU_Y), .en(ALU_WRITE), .clk(CLK), .Q(D_ALUOUT), .clr(RESET));
  Multiplexer #(.width(5), .select(2)) multiplexer_10 (
    .in0(IR[15:11]), .in1(IR[20:16]), .in2({5{1'b1}}), .in3({5{1'b0}}), .out(RF_RD), .sel(REG_DST));
  Multiplexer #(.width(32), .select(1)) multiplexer_11 (
    .in0(D_MDR_BYTE_ZEXT), .in1(D_MDR_BYTE_SEXT), .out(D_MDR_BYTE_EXT), .sel(MEM_SIGNED));
  Shifter #(.width(4), .shift("ll")) shifter_2 (.in(4'b0001), .\dist (D_ALUOUT[1:0]), .out(D_BYTE_MASK));
  assign D_IMM_SHAMT = {{27{1'b0}}, IR[10:6]};  // Bit_Extender bit_extender_3
  Register #(.width(32)) u_IR (.D(MEM_RDATA), .en(IR_WRITE), .clk(CLK), .Q(IR), .clr(RESET));
  Register #(.width(32)) u_B (.D(D_RD2), .en(B_WRITE), .clk(CLK), .Q(B), .clr(RESET));
  Register #(.width(32)) MDR (.D(MEM_RDATA), .en(MDR_WRITE), .clk(CLK), .Q(D_MDR), .clr(RESET));
  Multiplexer #(.width(32), .select(2)) multiplexer_12 (
    .in0(D_ALUOUT), .in1(D_LOAD_DATA), .in2({D_JUMP_TARGET, D_PC}), .in3({32{1'b0}}), .out(RF_WD),
    .sel(MEM_TO_REG));
  Multiplexer #(.width(32), .select(2)) multiplexer_13 (
    .in0(D_MDR), .in1(D_MDR_BYTE_EXT), .in2(D_MDR_BYTE_EXT), .in3(D_MDR_BYTE_EXT), .out(D_LOAD_DATA),
    .sel(MEM_SIZE));
  assign MEM_BE = D_MEM_BE_MASK & {4{MEM_WE}};  // AND_Gate and_1, 4 bits wide
  assign D_MDR_BYTE_ZEXT = {{24{1'b0}}, D_MDR_BYTE};  // Bit_Extender bit_extender_4
  Multiplexer #(.width(32), .select(2)) multiplexer_14 (
    .in0(B), .in1({B[7:0], B[7:0], B[7:0], B[7:0]}), .in2({B[7:0], B[7:0], B[7:0], B[7:0]}),
    .in3({B[7:0], B[7:0], B[7:0], B[7:0]}), .out(MEM_WDATA), .sel(MEM_SIZE));
  assign D_MDR_BYTE_SEXT = {{24{D_MDR_BYTE[7]}}, D_MDR_BYTE};  // Bit_Extender bit_extender_5

  assign TTY_DATA = B[6:0];

  // Other names for the same wires on the sheet: D_A[31:0] = A; D_ALU_ZERO = ALU_ZERO;
  //   D_ALUOUT_LO2[1:0] = D_ALUOUT[1:0]; D_B[31:0] = B; D_B_LO8[7:0] = B[7:0];
  //   D_BYTE_REP[31:0] = {B[7:0], B[7:0], B[7:0], B[7:0]}; D_IR[31:0] = IR; D_IMM16[15:0] = IR[15:0];
  //   D_IR26[25:0] = IR[25:0]; D_JUMP_TARGET[27:2] = IR[25:0]; D_SHAMT5[4:0] = IR[10:6]; D_RD_FIELD[4:0] = IR[15:11];
  //   D_RT_FIELD[4:0] = IR[20:16]; D_RS_FIELD[4:0] = IR[25:21]; D_PC[31:28] = D_JUMP_TARGET;
  //   D_PC_HI4[3:0] = D_JUMP_TARGET; D_MDR_B0[7:0] = D_MDR[7:0]; D_MDR_B1[7:0] = D_MDR[15:8];
  //   D_MDR_B2[7:0] = D_MDR[23:16]; D_MDR_B3[7:0] = D_MDR[31:24]; D_MEM_WE4[3:0] = {4{MEM_WE}}
endmodule

// VHDL entity Register_File, as the project stores it:
--------------------------------------------------------------------------------
-- Register_File: banco de 32 registros de 32 bits para S-MIPS.
--
-- Contrato Logisim<->VHDL (R16/R19):
--   * Entidad y subcircuito: Register_File
--   * Puertos std_logic / std_logic_vector, sin generics
--   * VHDL-2002, solo ieee.std_logic_1164 e ieee.numeric_std
--   * Sin wait, after, ficheros ni valores iniciales (R20)
--
-- Comportamiento:
--   * Dos lecturas combinacionales: RD1 = R[RS1], RD2 = R[RS2].
--   * $zero (registro 0) vale siempre 0; escribir en el se ignora.
--   * Escritura sincrona en el flanco de subida de CLK si REG_WRITE = 1.
--   * Reset asincrono activo alto: $gp = 0x00001800, $sp = 0x00003FFC,
--     el resto de registros a 0.
--------------------------------------------------------------------------------

library ieee;
use ieee.std_logic_1164.all;
use ieee.numeric_std.all;

entity Register_File is
  port (
    CLK       : in  std_logic;
    RESET     : in  std_logic;
    RS1       : in  std_logic_vector(4 downto 0);
    RS2       : in  std_logic_vector(4 downto 0);
    RD        : in  std_logic_vector(4 downto 0);
    WD        : in  std_logic_vector(31 downto 0);
    REG_WRITE : in  std_logic;
    RD1       : out std_logic_vector(31 downto 0);
    RD2       : out std_logic_vector(31 downto 0)
  );
end entity Register_File;

architecture rtl of Register_File is
  type reg_array is array (0 to 31) of std_logic_vector(31 downto 0);
  signal regs : reg_array;
begin

  -- Lectura combinacional. El registro $zero se fuerza a 0 aunque su
  -- contenido interno ya sea 0 por el reset y por la proteccion de escritura.
  RD1 <= (others => '0') when RS1 = "00000"
         else regs(to_integer(unsigned(RS1)));

  RD2 <= (others => '0') when RS2 = "00000"
         else regs(to_integer(unsigned(RS2)));

  -- Escritura y reset. RESET es asincrono y activo alto (R6).
  process (CLK, RESET)
  begin
    if RESET = '1' then
      for i in 0 to 31 loop
        regs(i) <= (others => '0');
      end loop;
      regs(28) <= x"00001800";  -- $gp
      regs(29) <= x"00003FFC";  -- $sp
    elsif rising_edge(CLK) then
      if REG_WRITE = '1' and RD /= "00000" then
        regs(to_integer(unsigned(RD))) <= WD;
      end if;
    end if;
  end process;

end architecture rtl;
